// Logisim project Practica02.circ as structural Verilog: 4 circuits, main circuit Implicación
module \Implicación  (
  input  in_1,
  input  Q,
  output out_3
);

  wire transistor_1_out;

  Transistor transistor_1 (.in(1'b1), .out(transistor_1_out), .gate(in_1));
  Transistor #(.\type ("n")) transistor_2 (.in(1'b0), .out(transistor_1_out), .gate(in_1));
  Transistor transistor_3 (.in(transistor_1_out), .out(out_3), .gate(Q));
  Transistor transistor_4 (.in(Q), .out(out_3), .gate(transistor_1_out));
  Transistor #(.\type ("n")) transistor_5 (.in(1'b1), .out(out_3), .gate(Q));

  // Notes on the sheet:
  //   ¬P
  //   NOT
  //   IMPLICACIÓN LÓGICA P -> Q = ¬P V Q
  //   OR
  //   SALIDA
endmodule

module Primos (
  input  in_1,
  input  in_2,
  input  in_3,
  output out_4
);

  wire and_1_out, and_2_out, not_1_out;

  not not_1 (not_1_out, in_1);
  and and_1 (and_1_out, in_3, in_1);
  and and_2 (and_2_out, in_2, not_1_out);
  or or_1 (out_4, and_1_out, and_2_out);

  // Notes on the sheet:
  //   NÚMEROS PRIMOS
endmodule

module Igualdad_XY (
  input  A,
  input  D,
  input  C,
  input  E,
  input  Y,
  input  B,
  output out_7
);

  wire AD_out, and_1_out, and_2_out, and_3_out, and_4_out, and_5_out, and_6_out, CF_out, nA_nD_out,
       nC_nF_out, not_1_out, not_2_out, not_3_out, not_4_out, not_5_out, not_6_out, or_1_out, or_3_out;

  and and_1 (and_1_out, B, and_2_out);
  and and_2 (and_2_out, E, or_3_out);
  and AD (AD_out, A, D);
  and and_3 (and_3_out, or_1_out, AD_out);
  or or_1 (or_1_out, and_1_out, and_6_out);
  or or_2 (out_7, and_3_out, and_4_out);
  not not_1 (not_1_out, D);
  not not_2 (not_2_out, A);
  and nA_nD (nA_nD_out, not_2_out, not_1_out);
  and and_4 (and_4_out, or_1_out, nA_nD_out);
  and CF (CF_out, C, Y);
  not not_3 (not_3_out, E);
  and and_5 (and_5_out, not_3_out, or_3_out);
  not not_4 (not_4_out, B);
  and and_6 (and_6_out, not_4_out, and_5_out);
  not not_5 (not_5_out, Y);
  not not_6 (not_6_out, C);
  and nC_nF (nC_nF_out, not_6_out, not_5_out);
  or or_3 (or_3_out, CF_out, nC_nF_out);

  // Notes on the sheet:
  //   X
  //   IGUALDAD ENTRE X, Y
  //   F
endmodule

module Menor_que_X_Y (
  input  A,
  input  B,
  input  C,
  input  D,
  input  E,
  input  F,
  output out_7
);

  wire A_nB_nC_out, A_nB_out, B_nc_out, D_nE_nFA_out, D_nEF_out, D_nEFA_out, DE_nF_out, DE_nfABC_nC_out,
       DE_out, DEF_out, DEFAB_out, DF_out, EF_nD_out, EF_out, nBC_out, nD_nEF_nA_nBC_out, nD_nEF_out,
       nD_nF_out, nDE_nF_out, nDE_nFA_nB_out, nDEFAC_out, nE_nF_out, nE_nFD_out, nEF_out, not_1_out,
       not_2_out, not_3_out, not_4_out, not_5_out, not_6_out, not_7_out, not_8_out, not_9_out, not_10_out,
       not_11_out, not_12_out, not_13_out, not_14_out, not_15_out, not_16_out, not_17_out, not_18_out,
       not_19_out, not_20_out, or_1_out, or_2_out, or_3_out, or_4_out, or_5_out;

  not not_1 (not_1_out, B);
  or or_1 (or_1_out, not_1_out, B_nc_out);
  or or_2 (or_2_out, or_1_out, not_4_out);
  not not_2 (not_2_out, B);
  and A_nB (A_nB_out, A, not_2_out);
  not not_3 (not_3_out, C);
  and B_nc (B_nc_out, B, not_3_out);
  not not_4 (not_4_out, A);
  and DEFAB (DEFAB_out, or_2_out, DEF_out);
  not not_5 (not_5_out, C);
  not not_6 (not_6_out, B);
  and A_nB_nC (A_nB_nC_out, A, not_6_out, not_5_out);
  not not_7 (not_7_out, A);
  or or_3 (or_3_out, not_7_out, A_nB_nC_out);
  not not_8 (not_8_out, A);
  not not_9 (not_9_out, B);
  not not_10 (not_10_out, C);
  and nBC (nBC_out, not_9_out, C);
  or or_4 (or_4_out, nBC_out, not_10_out);
  not not_11 (not_11_out, A);
  and nDEFAC (nDEFAC_out, not_11_out, or_4_out, EF_nD_out);
  not not_12 (not_12_out, A);
  or or_5 (or_5_out, not_8_out, A_nB_out);
  not not_13 (not_13_out, B);
  and nDE_nFA_nB (nDE_nFA_nB_out, not_12_out, not_13_out, nDE_nF_out);
  not not_14 (not_14_out, A);
  and D_nE_nFA (D_nE_nFA_out, not_14_out, nE_nFD_out);
  not not_15 (not_15_out, E);
  and nEF (nEF_out, F, not_15_out);
  and nD_nEF_nA_nBC (nD_nEF_nA_nBC_out, not_13_out, not_11_out, not_5_out, nD_nEF_out);
  and nD_nEF (nD_nEF_out, not_16_out, nEF_out);
  or or_6 (out_7, DEFAB_out, DE_nfABC_nC_out, D_nEFA_out, D_nE_nFA_out, nDEFAC_out, nDE_nFA_nB_out, nD_nEF_nA_nBC_out);
  and nD_nF (nD_nF_out, not_20_out, not_16_out);
  and nDE_nF (nDE_nF_out, E, nD_nF_out);
  and EF (EF_out, F, E);
  not not_16 (not_16_out, D);
  and EF_nD (EF_nD_out, EF_out, not_16_out);
  and DE (DE_out, D, E);
  and DF (DF_out, D, F);
  not not_17 (not_17_out, E);
  and DEF (DEF_out, DE_out, F);
  and D_nEF (D_nEF_out, DF_out, not_17_out);
  and D_nEFA (D_nEFA_out, or_3_out, D_nEF_out);
  not not_18 (not_18_out, F);
  not not_19 (not_19_out, E);
  and nE_nF (nE_nF_out, not_19_out, not_18_out);
  not not_20 (not_20_out, F);
  and DE_nF (DE_nF_out, DE_out, not_20_out);
  and DE_nfABC_nC (DE_nfABC_nC_out, or_5_out, DE_nF_out);
  and nE_nFD (nE_nFD_out, D, nE_nF_out);
endmodule
