// Logisim project Practica03.circ as structural Verilog: 7 circuits, main circuit Ejercicio 1- Un bit
module Ejercicio_1__Un_bit (
  input  in_1,
  input  in_2,
  input  in_3,
  output out_4
);

  wire and_1_out, or_1_out;

  and and_1 (and_1_out, in_1, in_2);
  or or_1 (or_1_out, in_1, in_2);
  Multiplexer #(.enable("false")) multiplexer_1 (.in0(and_1_out), .in1(or_1_out), .out(out_4), .sel(in_3));

  // Notes on the sheet:
  //   AND & OR
endmodule

module Ejercicio_2___Sumador (
  input  Carry_in,
  input  A,
  input  B,
  output Carry_Out,
  output Out
);

  wire and_1_out, and_2_out, and_3_out, and_4_out, and_5_out, and_6_out, and_7_out;

  and and_1 (and_1_out, Carry_in, A);
  and and_2 (and_2_out, B, ~Carry_in, A);  // AND_Gate
  and and_3 (and_3_out, B, Carry_in, ~A);  // AND_Gate
  and and_4 (and_4_out, ~A, ~Carry_in, B);  // AND_Gate
  and and_5 (and_5_out, A, ~Carry_in, ~B);  // AND_Gate
  and and_6 (and_6_out, Carry_in, ~A, ~B);  // AND_Gate
  and and_7 (and_7_out, Carry_in, A, B);
  or or_1 (Carry_Out, and_1_out, and_2_out, and_3_out);
  or or_2 (Out, and_4_out, and_5_out, and_6_out, and_7_out);

  // Notes on the sheet:
  //   SUMADOR
endmodule

module Ejercicio_3___Resta (
  input  Seleccionador1,
  input  Seleccionador0,
  input  A,
  input  B,
  input  Carry_In,
  output Out,
  output Carry_out
);

  wire and_1_out, and_2_out, multiplexer_1_out, not_1_out, or_1_out, Sumador_out;

  not not_1 (not_1_out, B);
  Multiplexer #(.enable("false")) multiplexer_1 (.in0(B), .in1(not_1_out), .out(multiplexer_1_out), .sel(and_2_out));
  and and_1 (and_1_out, A, B);
  or or_1 (or_1_out, A, B);
  Ejercicio_2___Sumador Sumador (
    .Carry_in(Carry_In), .A(A), .B(multiplexer_1_out), .Carry_Out(Carry_out), .Out(Sumador_out));
  and and_2 (and_2_out, Seleccionador1, Seleccionador0);
  Multiplexer #(.select(2), .enable("false")) multiplexer_2 (
    .in0(and_1_out), .in1(or_1_out), .in2(Sumador_out), .in3(Sumador_out), .out(Out),
    .sel({Seleccionador1, Seleccionador0}));

  // Notes on the sheet:
  //   RESTA
endmodule

module Ejercicio_4___ALU_8_bits (
  input  [1:0] Seleccionador,
  input  [7:0] A,
  input  [7:0] B,
  output [7:0] Salida,
  output Overflow
);

  wire and_1_out, ejercicio_3_resta_1_carry_out, ejercicio_3_resta_2_carry_out,
       ejercicio_3_resta_3_carry_out, ejercicio_3_resta_4_carry_out, ejercicio_3_resta_5_carry_out,
       ejercicio_3_resta_6_carry_out, ejercicio_3_resta_7_carry_out;

  Ejercicio_3___Resta ejercicio_3_resta_1 (
    .A(A[0]), .B(B[0]), .Carry_In(and_1_out), .Seleccionador1(Seleccionador[1]),
    .Seleccionador0(Seleccionador[0]), .Out(Salida[0]), .Carry_out(ejercicio_3_resta_1_carry_out));
  Ejercicio_3___Resta ejercicio_3_resta_2 (
    .A(A[1]), .B(B[1]), .Carry_In(ejercicio_3_resta_1_carry_out), .Seleccionador1(Seleccionador[1]),
    .Seleccionador0(Seleccionador[0]), .Out(Salida[1]), .Carry_out(ejercicio_3_resta_2_carry_out));
  Ejercicio_3___Resta ejercicio_3_resta_3 (
    .A(A[2]), .B(B[2]), .Carry_In(ejercicio_3_resta_2_carry_out), .Seleccionador1(Seleccionador[1]),
    .Seleccionador0(Seleccionador[0]), .Out(Salida[2]), .Carry_out(ejercicio_3_resta_3_carry_out));
  Ejercicio_3___Resta ejercicio_3_resta_4 (
    .A(A[3]), .B(B[3]), .Carry_In(ejercicio_3_resta_3_carry_out), .Seleccionador1(Seleccionador[1]),
    .Seleccionador0(Seleccionador[0]), .Out(Salida[3]), .Carry_out(ejercicio_3_resta_4_carry_out));
  Ejercicio_3___Resta ejercicio_3_resta_5 (
    .A(A[4]), .B(B[4]), .Carry_In(ejercicio_3_resta_4_carry_out), .Seleccionador1(Seleccionador[1]),
    .Seleccionador0(Seleccionador[0]), .Out(Salida[4]), .Carry_out(ejercicio_3_resta_5_carry_out));
  Ejercicio_3___Resta ejercicio_3_resta_6 (
    .A(A[5]), .B(B[5]), .Carry_In(ejercicio_3_resta_5_carry_out), .Seleccionador1(Seleccionador[1]),
    .Seleccionador0(Seleccionador[0]), .Out(Salida[5]), .Carry_out(ejercicio_3_resta_6_carry_out));
  Ejercicio_3___Resta ejercicio_3_resta_7 (
    .A(A[6]), .B(B[6]), .Carry_In(ejercicio_3_resta_6_carry_out), .Seleccionador1(Seleccionador[1]),
    .Seleccionador0(Seleccionador[0]), .Out(Salida[6]), .Carry_out(ejercicio_3_resta_7_carry_out));
  Ejercicio_3___Resta ejercicio_3_resta_8 (
    .A(A[7]), .B(B[7]), .Carry_In(ejercicio_3_resta_7_carry_out), .Seleccionador1(Seleccionador[1]),
    .Seleccionador0(Seleccionador[0]), .Out(Salida[7]), .Carry_out(Overflow));
  and and_1 (and_1_out, Seleccionador[1], Seleccionador[0]);

  // Notes on the sheet:
  //   A-B
endmodule

module Ejercicio_5___Igualdad (
  input  [2:0] Seleccionador,
  input  [7:0] A,
  input  [7:0] B,
  output IGUADAD,
  output [7:0] Salida,
  output Overflow
);

  wire and_1_out, and_2_out, ejercicio_3_resta_1_carry_out, ejercicio_3_resta_2_carry_out,
       ejercicio_3_resta_3_carry_out, ejercicio_3_resta_4_carry_out, ejercicio_3_resta_5_carry_out,
       ejercicio_3_resta_6_carry_out, ejercicio_3_resta_7_carry_out, or_1_out, or_2_out, or_3_out, or_4_out;
  wire [7:0] not_1_out;

  Ejercicio_3___Resta ejercicio_3_resta_1 (
    .A(A[0]), .B(B[0]), .Carry_In(or_4_out), .Seleccionador1(or_1_out), .Seleccionador0(or_3_out),
    .Out(Salida[0]), .Carry_out(ejercicio_3_resta_1_carry_out));
  Ejercicio_3___Resta ejercicio_3_resta_2 (
    .A(A[1]), .B(B[1]), .Carry_In(ejercicio_3_resta_1_carry_out), .Seleccionador1(or_1_out),
    .Seleccionador0(or_3_out), .Out(Salida[1]), .Carry_out(ejercicio_3_resta_2_carry_out));
  Ejercicio_3___Resta ejercicio_3_resta_3 (
    .A(A[2]), .B(B[2]), .Carry_In(ejercicio_3_resta_2_carry_out), .Seleccionador1(or_1_out),
    .Seleccionador0(or_3_out), .Out(Salida[2]), .Carry_out(ejercicio_3_resta_3_carry_out));
  Ejercicio_3___Resta ejercicio_3_resta_4 (
    .A(A[3]), .B(B[3]), .Carry_In(ejercicio_3_resta_3_carry_out), .Seleccionador1(or_1_out),
    .Seleccionador0(or_3_out), .Out(Salida[3]), .Carry_out(ejercicio_3_resta_4_carry_out));
  Ejercicio_3___Resta ejercicio_3_resta_5 (
    .A(A[4]), .B(B[4]), .Carry_In(ejercicio_3_resta_4_carry_out), .Seleccionador1(or_1_out),
    .Seleccionador0(or_3_out), .Out(Salida[4]), .Carry_out(ejercicio_3_resta_5_carry_out));
  Ejercicio_3___Resta ejercicio_3_resta_6 (
    .A(A[5]), .B(B[5]), .Carry_In(ejercicio_3_resta_5_carry_out), .Seleccionador1(or_1_out),
    .Seleccionador0(or_3_out), .Out(Salida[5]), .Carry_out(ejercicio_3_resta_6_carry_out));
  Ejercicio_3___Resta ejercicio_3_resta_7 (
    .A(A[6]), .B(B[6]), .Carry_In(ejercicio_3_resta_6_carry_out), .Seleccionador1(or_1_out),
    .Seleccionador0(or_3_out), .Out(Salida[6]), .Carry_out(ejercicio_3_resta_7_carry_out));
  Ejercicio_3___Resta ejercicio_3_resta_8 (
    .A(A[7]), .B(B[7]), .Carry_In(ejercicio_3_resta_7_carry_out), .Seleccionador1(or_1_out),
    .Seleccionador0(or_3_out), .Out(Salida[7]), .Carry_out(Overflow));
  or or_1 (or_1_out, or_4_out, Seleccionador[1]);
  or or_2 (or_2_out, Seleccionador[0], Seleccionador[1]);
  or or_3 (or_3_out, or_4_out, Seleccionador[0]);
  and and_1 (and_1_out, ~or_2_out, Seleccionador[2]);  // AND_Gate
  and and_2 (and_2_out, Seleccionador[0], Seleccionador[1]);
  or or_4 (or_4_out, and_1_out, and_2_out);
  assign not_1_out = ~Salida;  // NOT_Gate not_1, 8 bits wide
  and and_3 (IGUADAD, not_1_out[0], not_1_out[1], not_1_out[2], not_1_out[3], not_1_out[4], not_1_out[5], not_1_out[6], not_1_out[7]);

  // Notes on the sheet:
  //   A==B?
endmodule

module Ejercicio_6___Nor (
  input  [2:0] Seleccionador,
  input  [7:0] A,
  input  [7:0] B,
  output IGUADAD,
  output [7:0] Salida,
  output Overflow
);

  wire and_1_out, and_2_out, and_3_out, ejercicio_3_resta_1_carry_out, ejercicio_3_resta_2_carry_out,
       ejercicio_3_resta_3_carry_out, ejercicio_3_resta_4_carry_out, ejercicio_3_resta_5_carry_out,
       ejercicio_3_resta_6_carry_out, ejercicio_3_resta_7_carry_out, or_1_out, or_2_out, or_3_out, or_4_out;
  wire [7:0] ejercicio_3_resta_1_out, not_1_out, not_2_out;

  Ejercicio_3___Resta ejercicio_3_resta_1 (
    .A(A[0]), .B(B[0]), .Carry_In(or_4_out), .Seleccionador1(or_1_out), .Seleccionador0(or_3_out),
    .Out(ejercicio_3_resta_1_out[0]), .Carry_out(ejercicio_3_resta_1_carry_out));
  Ejercicio_3___Resta ejercicio_3_resta_2 (
    .A(A[1]), .B(B[1]), .Carry_In(ejercicio_3_resta_1_carry_out), .Seleccionador1(or_1_out),
    .Seleccionador0(or_3_out), .Out(ejercicio_3_resta_1_out[1]), .Carry_out(ejercicio_3_resta_2_carry_out));
  Ejercicio_3___Resta ejercicio_3_resta_3 (
    .A(A[2]), .B(B[2]), .Carry_In(ejercicio_3_resta_2_carry_out), .Seleccionador1(or_1_out),
    .Seleccionador0(or_3_out), .Out(ejercicio_3_resta_1_out[2]), .Carry_out(ejercicio_3_resta_3_carry_out));
  Ejercicio_3___Resta ejercicio_3_resta_4 (
    .A(A[3]), .B(B[3]), .Carry_In(ejercicio_3_resta_3_carry_out), .Seleccionador1(or_1_out),
    .Seleccionador0(or_3_out), .Out(ejercicio_3_resta_1_out[3]), .Carry_out(ejercicio_3_resta_4_carry_out));
  Ejercicio_3___Resta ejercicio_3_resta_5 (
    .A(A[4]), .B(B[4]), .Carry_In(ejercicio_3_resta_4_carry_out), .Seleccionador1(or_1_out),
    .Seleccionador0(or_3_out), .Out(ejercicio_3_resta_1_out[4]), .Carry_out(ejercicio_3_resta_5_carry_out));
  Ejercicio_3___Resta ejercicio_3_resta_6 (
    .A(A[5]), .B(B[5]), .Carry_In(ejercicio_3_resta_5_carry_out), .Seleccionador1(or_1_out),
    .Seleccionador0(or_3_out), .Out(ejercicio_3_resta_1_out[5]), .Carry_out(ejercicio_3_resta_6_carry_out));
  Ejercicio_3___Resta ejercicio_3_resta_7 (
    .A(A[6]), .B(B[6]), .Carry_In(ejercicio_3_resta_6_carry_out), .Seleccionador1(or_1_out),
    .Seleccionador0(or_3_out), .Out(ejercicio_3_resta_1_out[6]), .Carry_out(ejercicio_3_resta_7_carry_out));
  Ejercicio_3___Resta ejercicio_3_resta_8 (
    .A(A[7]), .B(B[7]), .Carry_In(ejercicio_3_resta_7_carry_out), .Seleccionador1(or_1_out),
    .Seleccionador0(or_3_out), .Out(ejercicio_3_resta_1_out[7]), .Carry_out(Overflow));
  or or_1 (or_1_out, or_4_out, Seleccionador[1]);
  or or_2 (or_2_out, Seleccionador[0], Seleccionador[1]);
  or or_3 (or_3_out, or_4_out, Seleccionador[0]);
  and and_1 (and_1_out, ~or_2_out, Seleccionador[2]);  // AND_Gate
  and and_2 (and_2_out, Seleccionador[0], Seleccionador[1]);
  or or_4 (or_4_out, and_1_out, and_2_out);
  and and_3 (and_3_out, Seleccionador[2], Seleccionador[0]);
  assign not_1_out = ~ejercicio_3_resta_1_out;  // NOT_Gate not_1, 8 bits wide
  assign not_2_out = ~ejercicio_3_resta_1_out;  // NOT_Gate not_2, 8 bits wide
  Multiplexer #(.width(8), .enable("false")) multiplexer_1 (
    .in0(ejercicio_3_resta_1_out), .in1(not_2_out), .out(Salida), .sel(and_3_out));
  and and_4 (IGUADAD, not_1_out[0], not_1_out[1], not_1_out[2], not_1_out[3], not_1_out[4], not_1_out[5], not_1_out[6], not_1_out[7]);

  // Notes on the sheet:
  //   NOR
endmodule

module Main (
  input  [2:0] \OPERACIÓN ,
  input  [7:0] A,
  input  [7:0] B,
  output IGUALDAD,
  output [7:0] SALIDA,
  output OVERFLOW
);

  Ejercicio_6___Nor ejercicio_6_nor_1 (
    .Seleccionador(\OPERACIÓN ), .A(A), .B(B), .Overflow(OVERFLOW), .IGUADAD(IGUALDAD), .Salida(SALIDA));

  // Notes on the sheet:
  //   MAIN
endmodule
