// Logisim project Ejemplo Circuito Secuencial.circ as structural Verilog: 2 circuits, main circuit Funcionamiento Flip Flops
module Funcionamiento_Flip_Flops (
  input  in_1,
  input  in_2,
  input  in_3,
  input  in_4,
  input  in_5,
  input  in_6,
  output out_7,
  output out_8,
  output out_9,
  output out_10,
  output out_11,
  output out_12,
  output out_13,
  output out_14
);

  wire clock_1_out;

  Clock clock_1 (.out(clock_1_out));
  D_Flip_Flop d_ff_1 (.clk(clock_1_out), .D(in_1), .Q(out_7), .Qn(out_8), .en(1'b1));  // open: preset, reset
  T_Flip_Flop t_ff_1 (.clk(clock_1_out), .T(in_2), .Q(out_9), .Qn(out_10), .en(1'b1));  // open: preset, reset
  J_K_Flip_Flop j_k_ff_1 (
    .J(in_3), .clk(clock_1_out), .K(in_4), .Q(out_11), .Qn(out_12), .en(1'b1));  // open: preset, reset
  S_R_Flip_Flop s_r_ff_1 (
    .S(in_5), .clk(clock_1_out), .R(in_6), .Q(out_13), .Qn(out_14), .en(1'b1));  // open: preset, reset
endmodule

module Ejemplo_circuito_Secuencial (
  input  in_1
);

  wire and_1_out, and_2_out, and_3_out, clock_1_out, d_ff_1_q, d_ff_1_qn, d_ff_2_q, d_ff_2_qn, not_1_out,
       or_1_out;

  Clock clock_1 (.out(clock_1_out));
  D_Flip_Flop d_ff_1 (.clk(clock_1_out), .D(or_1_out), .Q(d_ff_1_q), .Qn(d_ff_1_qn), .en(1'b1));  // open: preset, reset
  D_Flip_Flop d_ff_2 (
    .clk(clock_1_out), .D(and_3_out), .Q(d_ff_2_q), .Qn(d_ff_2_qn), .en(1'b1));  // open: preset, reset
  or or_1 (or_1_out, and_1_out, and_2_out);
  not not_1 (not_1_out, in_1);
  and and_1 (and_1_out, d_ff_2_qn, in_1);
  and and_2 (and_2_out, d_ff_1_qn, d_ff_2_q, not_1_out);
  and and_3 (and_3_out, d_ff_2_qn, d_ff_1_qn, not_1_out);
endmodule
