// Logisim project Practica04.circ as structural Verilog: 9 circuits, main circuit Ejercicio-1 Contador
module Ejercicio_1_Contador (
);

  wire and_1_out, and_2_out, and_3_out, and_4_out, and_5_out, clock_1_out, not_1_out, or_1_out, t_ff_1_qn;
  wire [3:0] t_ff_1_q;

  Clock clock_1 (.out(clock_1_out));
  not not_1 (not_1_out, t_ff_1_qn);
  and and_1 (and_1_out, not_1_out, ~and_5_out);  // AND_Gate
  and and_2 (and_2_out, t_ff_1_q[1], t_ff_1_q[0]);
  and and_3 (and_3_out, and_2_out, ~and_5_out);  // AND_Gate
  and and_4 (and_4_out, and_2_out, t_ff_1_q[2]);
  T_Flip_Flop t_ff_1 (
    .clk(clock_1_out), .T(clock_1_out), .Q(t_ff_1_q[0]), .Qn(t_ff_1_qn), .en(1'b1));  // open: preset, reset
  T_Flip_Flop t_ff_2 (.clk(clock_1_out), .T(and_1_out), .Q(t_ff_1_q[1]), .en(1'b1));  // open: Qn, preset, reset
  T_Flip_Flop t_ff_3 (.clk(clock_1_out), .T(and_3_out), .Q(t_ff_1_q[2]), .en(1'b1));  // open: Qn, preset, reset
  T_Flip_Flop t_ff_4 (.clk(clock_1_out), .T(or_1_out), .Q(t_ff_1_q[3]), .en(1'b1));  // open: Qn, preset, reset
  or or_1 (or_1_out, and_4_out, and_5_out);
  and and_5 (and_5_out, t_ff_1_q[3], t_ff_1_q[0]);
  Hex_Digit_Display hex_digit_display_1 (.value(t_ff_1_q));  // open: dp
endmodule

module PtoExtra___Contador_999 (
);

  wire and_1_out, and_2_out, and_3_out, and_4_out, and_5_out, and_6_out, and_7_out, and_8_out, and_9_out,
       and_10_out, and_11_out, and_12_out, and_13_out, and_14_out, and_15_out, and_16_out, and_17_out,
       clock_1_out, or_1_out, or_2_out, or_3_out, t_ff_1_qn, t_ff_2_qn, t_ff_9_qn;
  wire [3:0] t_ff_1_q, t_ff_2_q, t_ff_9_q;

  Clock clock_1 (.out(clock_1_out));
  and and_1 (and_1_out, ~t_ff_9_q[0], clock_1_out, and_16_out);  // AND_Gate
  and and_2 (and_2_out, t_ff_1_q[0], t_ff_1_q[3]);
  T_Flip_Flop t_ff_1 (
    .clk(clock_1_out), .T(clock_1_out), .Q(t_ff_1_q[0]), .Qn(t_ff_1_qn), .en(1'b1));  // open: preset, reset
  and and_3 (and_3_out, ~t_ff_1_qn, ~and_2_out);  // AND_Gate
  and and_4 (and_4_out, t_ff_1_q[1], t_ff_1_q[0]);
  and and_5 (and_5_out, and_4_out, ~and_2_out);  // AND_Gate
  and and_6 (and_6_out, and_4_out, t_ff_1_q[2]);
  or or_1 (or_1_out, and_6_out, and_2_out);
  T_Flip_Flop t_ff_2 (
    .clk(and_1_out), .T(and_1_out), .Q(t_ff_2_q[0]), .Qn(t_ff_2_qn), .en(1'b1));  // open: preset, reset
  and and_7 (and_7_out, ~t_ff_2_qn, ~and_11_out);  // AND_Gate
  and and_8 (and_8_out, t_ff_2_q[1], t_ff_2_q[0]);
  and and_9 (and_9_out, and_8_out, ~and_11_out);  // AND_Gate
  and and_10 (and_10_out, and_8_out, t_ff_2_q[2]);
  and and_11 (and_11_out, t_ff_2_q[0], t_ff_2_q[3]);
  or or_2 (or_2_out, and_10_out, and_11_out);
  T_Flip_Flop t_ff_3 (.clk(clock_1_out), .T(and_3_out), .Q(t_ff_1_q[1]), .en(1'b1));  // open: Qn, preset, reset
  T_Flip_Flop t_ff_4 (.clk(clock_1_out), .T(and_5_out), .Q(t_ff_1_q[2]), .en(1'b1));  // open: Qn, preset, reset
  T_Flip_Flop t_ff_5 (.clk(clock_1_out), .T(or_1_out), .Q(t_ff_1_q[3]), .en(1'b1));  // open: Qn, preset, reset
  T_Flip_Flop t_ff_6 (.clk(and_1_out), .T(and_7_out), .Q(t_ff_2_q[1]), .en(1'b1));  // open: Qn, preset, reset
  T_Flip_Flop t_ff_7 (.clk(and_1_out), .T(and_9_out), .Q(t_ff_2_q[2]), .en(1'b1));  // open: Qn, preset, reset
  T_Flip_Flop t_ff_8 (.clk(and_1_out), .T(or_2_out), .Q(t_ff_2_q[3]), .en(1'b1));  // open: Qn, preset, reset
  and and_12 (and_12_out, ~t_ff_1_q[0], and_2_out, clock_1_out);  // AND_Gate
  and and_13 (and_13_out, ~t_ff_9_qn, ~and_16_out);  // AND_Gate
  and and_14 (and_14_out, t_ff_9_q[1], t_ff_9_q[0]);
  and and_15 (and_15_out, and_14_out, ~and_16_out);  // AND_Gate
  and and_16 (and_16_out, t_ff_9_q[0], t_ff_9_q[3]);
  T_Flip_Flop t_ff_9 (
    .clk(and_12_out), .T(and_12_out), .Q(t_ff_9_q[0]), .Qn(t_ff_9_qn), .en(1'b1));  // open: preset, reset
  and and_17 (and_17_out, and_14_out, t_ff_9_q[2]);
  or or_3 (or_3_out, and_17_out, and_16_out);
  T_Flip_Flop t_ff_10 (.clk(and_12_out), .T(and_13_out), .Q(t_ff_9_q[1]), .en(1'b1));  // open: Qn, preset, reset
  T_Flip_Flop t_ff_11 (.clk(and_12_out), .T(and_15_out), .Q(t_ff_9_q[2]), .en(1'b1));  // open: Qn, preset, reset
  T_Flip_Flop t_ff_12 (.clk(and_12_out), .T(or_3_out), .Q(t_ff_9_q[3]), .en(1'b1));  // open: Qn, preset, reset
  Hex_Digit_Display hex_digit_display_1 (.value(t_ff_9_q));  // open: dp
  Hex_Digit_Display hex_digit_display_2 (.value(t_ff_2_q));  // open: dp
  Hex_Digit_Display hex_digit_display_3 (.value(t_ff_1_q));  // open: dp
endmodule

module Ejercicio_2_Automata (
  input  X
);

  wire A_q, A_qn, AB_out, B_q, clock_1_out, not_1_out, nX_nA_out, nXB_out, or_1_out, or_2_out;

  Clock clock_1 (.out(clock_1_out));
  not not_1 (not_1_out, X);
  D_Flip_Flop A (.clk(clock_1_out), .D(or_1_out), .Q(A_q), .Qn(A_qn), .en(1'b1));  // open: preset, reset
  D_Flip_Flop B (.clk(clock_1_out), .D(or_2_out), .Q(B_q), .en(1'b1));  // open: Qn, preset, reset
  or or_1 (or_1_out, nXB_out, AB_out);
  or or_2 (or_2_out, nX_nA_out, AB_out);
  and nX_nA (nX_nA_out, not_1_out, A_qn);
  and nXB (nXB_out, not_1_out, B_q);
  and AB (AB_out, X, A_q);

  // Notes on the sheet:
  //   A | B | X | A+1 | B+1
  //         0 |0  | 0   | 0   |   1  
  //         0 |0  | 1   | 0   |   0  
  //         0 |1  | 0   | 1   |   1  
  //         0 |1  | 1   | 0   |   0  
  //         1 |0  | 0   | 0   |   0  
  //         1 |0  | 1   |  1  |   1  
  //         1 |1  | 0   | 1   |   0  
  //         1 |1  | 1   | 1   |   1  
  //   T = 00
  //   TE = 01
  //   NTE = 10
  //   NT = 11
endmodule

module Registro_Flip_Flop_D (
  input  Reloj,
  input  [7:0] Entrada,
  output [7:0] Salida
);

  D_Flip_Flop d_ff_1 (.clk(Reloj), .D(Entrada[0]), .Q(Salida[0]), .en(1'b1));  // open: Qn, preset, reset
  D_Flip_Flop d_ff_2 (.clk(Reloj), .D(Entrada[1]), .Q(Salida[1]), .en(1'b1));  // open: Qn, preset, reset
  D_Flip_Flop d_ff_3 (.clk(Reloj), .D(Entrada[2]), .Q(Salida[2]), .en(1'b1));  // open: Qn, preset, reset
  D_Flip_Flop d_ff_4 (.clk(Reloj), .D(Entrada[3]), .Q(Salida[3]), .en(1'b1));  // open: Qn, preset, reset
  D_Flip_Flop d_ff_5 (.clk(Reloj), .D(Entrada[4]), .Q(Salida[4]), .en(1'b1));  // open: Qn, preset, reset
  D_Flip_Flop d_ff_6 (.clk(Reloj), .D(Entrada[5]), .Q(Salida[5]), .en(1'b1));  // open: Qn, preset, reset
  D_Flip_Flop d_ff_7 (.clk(Reloj), .D(Entrada[6]), .Q(Salida[6]), .en(1'b1));  // open: Qn, preset, reset
  D_Flip_Flop d_ff_8 (.clk(Reloj), .D(Entrada[7]), .Q(Salida[7]), .en(1'b1));  // open: Qn, preset, reset
endmodule

// REG-FILE
module Ejercicio_3_Register_file (
  input  [1:0] Read_register_number_1,
  input  [1:0] Read_register_number_2,
  input  [7:0] Write_data,
  input  [1:0] Write_register,
  input  Write,
  output [7:0] Read_data_1,
  output [7:0] Read_data_2
);

  wire and_1_out, and_2_out, and_3_out, and_4_out;
  wire [7:0] demultiplexer_1_out0, demultiplexer_1_out1, demultiplexer_1_out2, demultiplexer_1_out3,
       registro_ff_d_1_salida, registro_ff_d_2_salida, registro_ff_d_3_salida, registro_ff_d_4_salida;

  Demultiplexer #(.select(2), .width(8), .enable("false")) demultiplexer_1 (
    .out0(demultiplexer_1_out0), .out1(demultiplexer_1_out1), .out2(demultiplexer_1_out2),
    .out3(demultiplexer_1_out3), .in(Write_data), .sel(Write_register));
  and and_1 (and_1_out, ~Write_register[0], ~Write_register[1], Write);  // AND_Gate
  and and_2 (and_2_out, Write_register[0], ~Write_register[1], Write);  // AND_Gate
  Registro_Flip_Flop_D registro_ff_d_1 (
    .Reloj(and_1_out), .Entrada(demultiplexer_1_out0), .Salida(registro_ff_d_1_salida));
  Registro_Flip_Flop_D registro_ff_d_2 (
    .Reloj(and_2_out), .Entrada(demultiplexer_1_out1), .Salida(registro_ff_d_2_salida));
  and and_3 (and_3_out, ~Write_register[0], Write_register[1], Write);  // AND_Gate
  Registro_Flip_Flop_D registro_ff_d_3 (
    .Reloj(and_3_out), .Entrada(demultiplexer_1_out2), .Salida(registro_ff_d_3_salida));
  and and_4 (and_4_out, Write_register[0], Write_register[1], Write);
  Registro_Flip_Flop_D registro_ff_d_4 (
    .Reloj(and_4_out), .Entrada(demultiplexer_1_out3), .Salida(registro_ff_d_4_salida));
  Multiplexer #(.select(2), .width(8), .enable("false")) multiplexer_1 (
    .in0(registro_ff_d_1_salida), .in1(registro_ff_d_2_salida), .in2(registro_ff_d_3_salida),
    .in3(registro_ff_d_4_salida), .out(Read_data_1), .sel(Read_register_number_1));
  Multiplexer #(.select(2), .width(8), .enable("false")) multiplexer_2 (
    .in0(registro_ff_d_1_salida), .in1(registro_ff_d_2_salida), .in2(registro_ff_d_3_salida),
    .in3(registro_ff_d_4_salida), .out(Read_data_2), .sel(Read_register_number_2));
endmodule

module Ejercicio_4_ALU_REG_fILE (
  input  [2:0] Operacion,
  input  Segundo_operando,
  input  [1:0] No__Registro_1,
  input  [1:0] No__Registro_2,
  input  [7:0] \Número_inmediato ,
  input  [1:0] Register_file,
  output Igualdad,
  output Overflow,
  output [7:0] Resultado
);

  wire clock_1_out;
  wire [7:0] ejercicio_3_register_file_1_read_data_1, ejercicio_3_register_file_1_read_data_2,
       multiplexer_1_out;

  Multiplexer #(.width(8), .enable("false")) multiplexer_1 (
    .in0(Resultado), .in1(\Número_inmediato ), .out(multiplexer_1_out), .sel(Segundo_operando));
  Ejercicio_3_Register_file ejercicio_3_register_file_1 (
    .Read_register_number_1(No__Registro_1), .Read_register_number_2(No__Registro_2),
    .Write_data(multiplexer_1_out), .Write_register(Register_file), .Write(clock_1_out),
    .Read_data_1(ejercicio_3_register_file_1_read_data_1),
    .Read_data_2(ejercicio_3_register_file_1_read_data_2));
  Clock clock_1 (.out(clock_1_out));
  Practica3_ALU_8bits_Igualdad practica3_alu_8bits_igualdad_1 (
    .Seleccionador(Operacion), .A(ejercicio_3_register_file_1_read_data_1),
    .B(ejercicio_3_register_file_1_read_data_2), .Overflow(Overflow), .IGUADAD(Igualdad), .Salida(Resultado));
endmodule

module Practica3_Sumador (
  input  Carry_in,
  input  A,
  input  B,
  output Carry_Out,
  output Out
);

  wire and_1_out, and_2_out, and_3_out, and_4_out, and_5_out, and_6_out, and_7_out;

  and and_1 (and_1_out, Carry_in, A);
  and and_2 (and_2_out, B, ~Carry_in, A);  // AND_Gate
  and and_3 (and_3_out, B, Carry_in, ~A);  // AND_Gate
  and and_4 (and_4_out, ~A, ~Carry_in, B);  // AND_Gate
  and and_5 (and_5_out, A, ~Carry_in, ~B);  // AND_Gate
  and and_6 (and_6_out, Carry_in, ~A, ~B);  // AND_Gate
  and and_7 (and_7_out, Carry_in, A, B);
  or or_1 (Carry_Out, and_1_out, and_2_out, and_3_out);
  or or_2 (Out, and_4_out, and_5_out, and_6_out, and_7_out);

  // Notes on the sheet:
  //   SUMADOR
endmodule

module Practica3_Resta (
  input  Seleccionador1,
  input  Seleccionador0,
  input  A,
  input  B,
  input  Carry_In,
  output Out,
  output Carry_out
);

  wire and_1_out, and_2_out, multiplexer_1_out, not_1_out, or_1_out, practica3_sumador_1_out;

  not not_1 (not_1_out, B);
  Multiplexer #(.enable("false")) multiplexer_1 (.in0(B), .in1(not_1_out), .out(multiplexer_1_out), .sel(and_2_out));
  and and_1 (and_1_out, A, B);
  or or_1 (or_1_out, A, B);
  Practica3_Sumador practica3_sumador_1 (
    .Carry_in(Carry_In), .A(A), .B(multiplexer_1_out), .Carry_Out(Carry_out), .Out(practica3_sumador_1_out));
  and and_2 (and_2_out, Seleccionador1, Seleccionador0);
  Multiplexer #(.select(2), .enable("false")) multiplexer_2 (
    .in0(and_1_out), .in1(or_1_out), .in2(practica3_sumador_1_out), .in3(practica3_sumador_1_out), .out(Out),
    .sel({Seleccionador1, Seleccionador0}));

  // Notes on the sheet:
  //   RESTA
endmodule

// ALU
module Practica3_ALU_8bits_Igualdad (
  input  [2:0] Seleccionador,
  input  [7:0] A,
  input  [7:0] B,
  output IGUADAD,
  output [7:0] Salida,
  output Overflow
);

  wire and_1_out, and_2_out, or_1_out, or_2_out, or_3_out, or_4_out, practica3_resta_1_carry_out,
       practica3_resta_2_carry_out, practica3_resta_3_carry_out, practica3_resta_4_carry_out,
       practica3_resta_5_carry_out, practica3_resta_6_carry_out, practica3_resta_7_carry_out;
  wire [7:0] not_1_out;

  Practica3_Resta practica3_resta_1 (
    .A(A[0]), .B(B[0]), .Carry_In(or_4_out), .Seleccionador1(or_1_out), .Seleccionador0(or_3_out),
    .Out(Salida[0]), .Carry_out(practica3_resta_1_carry_out));
  Practica3_Resta practica3_resta_2 (
    .A(A[1]), .B(B[1]), .Carry_In(practica3_resta_1_carry_out), .Seleccionador1(or_1_out),
    .Seleccionador0(or_3_out), .Out(Salida[1]), .Carry_out(practica3_resta_2_carry_out));
  Practica3_Resta practica3_resta_3 (
    .A(A[2]), .B(B[2]), .Carry_In(practica3_resta_2_carry_out), .Seleccionador1(or_1_out),
    .Seleccionador0(or_3_out), .Out(Salida[2]), .Carry_out(practica3_resta_3_carry_out));
  Practica3_Resta practica3_resta_4 (
    .A(A[3]), .B(B[3]), .Carry_In(practica3_resta_3_carry_out), .Seleccionador1(or_1_out),
    .Seleccionador0(or_3_out), .Out(Salida[3]), .Carry_out(practica3_resta_4_carry_out));
  Practica3_Resta practica3_resta_5 (
    .A(A[4]), .B(B[4]), .Carry_In(practica3_resta_4_carry_out), .Seleccionador1(or_1_out),
    .Seleccionador0(or_3_out), .Out(Salida[4]), .Carry_out(practica3_resta_5_carry_out));
  Practica3_Resta practica3_resta_6 (
    .A(A[5]), .B(B[5]), .Carry_In(practica3_resta_5_carry_out), .Seleccionador1(or_1_out),
    .Seleccionador0(or_3_out), .Out(Salida[5]), .Carry_out(practica3_resta_6_carry_out));
  Practica3_Resta practica3_resta_7 (
    .A(A[6]), .B(B[6]), .Carry_In(practica3_resta_6_carry_out), .Seleccionador1(or_1_out),
    .Seleccionador0(or_3_out), .Out(Salida[6]), .Carry_out(practica3_resta_7_carry_out));
  Practica3_Resta practica3_resta_8 (
    .A(A[7]), .B(B[7]), .Carry_In(practica3_resta_7_carry_out), .Seleccionador1(or_1_out),
    .Seleccionador0(or_3_out), .Out(Salida[7]), .Carry_out(Overflow));
  or or_1 (or_1_out, or_4_out, Seleccionador[1]);
  or or_2 (or_2_out, Seleccionador[0], Seleccionador[1]);
  or or_3 (or_3_out, or_4_out, Seleccionador[0]);
  and and_1 (and_1_out, ~or_2_out, Seleccionador[2]);  // AND_Gate
  and and_2 (and_2_out, Seleccionador[0], Seleccionador[1]);
  or or_4 (or_4_out, and_1_out, and_2_out);
  assign not_1_out = ~Salida;  // NOT_Gate not_1, 8 bits wide
  and and_3 (IGUADAD, not_1_out[0], not_1_out[1], not_1_out[2], not_1_out[3], not_1_out[4], not_1_out[5], not_1_out[6], not_1_out[7]);

  // Notes on the sheet:
  //   A==B?
endmodule
